// Logisim project clock_module.circ as structural Verilog: 1 circuit, main circuit main
module main (
);

  wire and_1_out, and_2_out, button_1_out, Clock, clock_1_out, dipswitch_1_p1, dipswitch_1_p2, not_1_out,
       not_2_out, or_1_out;

  // DipSwitch #(.number(2)) dipswitch_1: pin names not known; wires that end beside it: dipswitch_1_p1, dipswitch_1_p2
  Button button_1 (.out(button_1_out));
  Clock clock_1 (.out(clock_1_out));
  not not_1 (not_1_out, dipswitch_1_p1);
  not not_2 (not_2_out, dipswitch_1_p2);
  and and_1 (and_1_out, button_1_out, dipswitch_1_p1);
  and and_2 (and_2_out, not_1_out, clock_1_out);
  or or_1 (or_1_out, and_1_out, and_2_out);
  and and_3 (Clock, or_1_out, not_2_out);
endmodule
