// Logisim project test.circ as structural Verilog: 1 circuit, main circuit main
module main (
  input  [7:0] in_1,
  input  [7:0] in_2
);

  wire and_1_out, and_2_out, and_3_out, clock_1_out, dipswitch_1_p1, dipswitch_1_p2, dipswitch_1_p3,
       dipswitch_1_p4, dipswitch_1_p5, dipswitch_1_p6, dipswitch_1_p7, dipswitch_1_p8, dipswitch_2_p1,
       dipswitch_2_p2, not_1_out, not_2_out, not_3_out, not_4_out;
  wire [7:0] ram_1_dout;

  // DipSwitch dipswitch_1: pin names not known; wires that end beside it: dipswitch_1_p1, dipswitch_1_p2, dipswitch_1_p3, dipswitch_1_p4, dipswitch_1_p5, dipswitch_1_p6, dipswitch_1_p7, dipswitch_1_p8
  Clock clock_1 (.out(clock_1_out));
  not not_1 (not_1_out, dipswitch_1_p5);
  not not_2 (not_2_out, dipswitch_1_p6);
  not not_3 (not_3_out, dipswitch_1_p7);
  not not_4 (not_4_out, dipswitch_1_p8);
  // DipSwitch #(.number(2)) dipswitch_2: pin names not known; wires that end beside it: dipswitch_2_p1, dipswitch_2_p2
  and and_1 (and_1_out, dipswitch_1_p1, dipswitch_1_p2, dipswitch_1_p3, dipswitch_1_p4);
  and and_2 (and_2_out, not_1_out, not_2_out, not_3_out, not_4_out);
  RAM ram_1 (.addr(in_1), .we(dipswitch_2_p1), .oe(dipswitch_2_p2), .clk(clock_1_out), .din(in_2), .dout(ram_1_dout));
  and and_3 (and_3_out, and_1_out, and_2_out);
  LedBar ledbar_1 (
    .led0(ram_1_dout[0]), .led1(ram_1_dout[1]), .led2(ram_1_dout[2]), .led3(ram_1_dout[3]),
    .led4(ram_1_dout[4]), .led5(ram_1_dout[5]), .led6(ram_1_dout[6]), .led7(ram_1_dout[7]));
endmodule
